# Fritzing sketch bt_rgb (saved by Fritzing 0.9.3b)
breadboards: 1

parts:
  RBG_LED = RGB LED (com. cathode, rgb) [package="5 mm [THT]"]
  Arduino = Arduino Uno (Rev3)
  HC-06 = Bluetooth HC-05 Macho
  R1 = Resistor [tolerance=±5% resistance=1k package=THT]
  R2 = Resistor [tolerance=±5% resistance=1k package=THT]
  R3 = Resistor [tolerance=±5% resistance=1k package=THT]

nets:
  N1: RBG_LED.red_anode, Arduino.D3_PWM
  GND: RBG_LED.common_cathode, Arduino.GND, HC-06.GND, R3.Pin_1
  N2: RBG_LED.green_anode, Arduino.D5_PWM
  N3: RBG_LED.blue_anode, Arduino.D6_PWM
  N4: Arduino.D0/RX, HC-06.RXD
  N5: Arduino.D1/TX, R1.Pin_0
  5V: Arduino.5V, HC-06.VCC
  N6: HC-06.TXD, R1.Pin_1, R2.Pin_0
  N7: R2.Pin_1, R3.Pin_0
